// Logisim project 7 bit resister.circ as structural Verilog: 1 circuit, main circuit main
module main (
  input  LOAD,
  input  INC,
  input  CLK,
  input  CLR,
  input  [6:0] INPUT,
  output [6:0] OUTPUT
);

  wire and_1_out, and_2_out, and_3_out, and_4_out, and_5_out, and_6_out, and_7_out, and_8_out, and_9_out,
       and_10_out, and_11_out, and_12_out, and_13_out, and_14_out, and_15_out, and_16_out, and_17_out,
       and_18_out, and_19_out, and_20_out, and_21_out, and_22_out, not_1_out, not_2_out, not_3_out,
       not_4_out, not_5_out, not_6_out, not_7_out, not_8_out, or_1_out, or_2_out, or_3_out, or_4_out,
       or_5_out, or_6_out, or_7_out, or_8_out, or_9_out, or_10_out, or_11_out, or_12_out, or_13_out,
       or_14_out;

  and and_1 (and_1_out, LOAD, LOAD);
  not not_1 (not_1_out, LOAD);
  not not_2 (not_2_out, INPUT[1]);
  not not_3 (not_3_out, INPUT[2]);
  not not_4 (not_4_out, INPUT[3]);
  not not_5 (not_5_out, INPUT[4]);
  not not_6 (not_6_out, INPUT[5]);
  not not_7 (not_7_out, INPUT[6]);
  and and_2 (and_2_out, not_1_out, not_1_out, INC);
  not not_8 (not_8_out, INPUT[0]);
  and and_3 (and_3_out, and_1_out, INPUT[0]);
  and and_4 (and_4_out, and_1_out, not_8_out);
  and and_5 (and_5_out, and_1_out, INPUT[1]);
  and and_6 (and_6_out, and_1_out, not_2_out);
  and and_7 (and_7_out, and_1_out, INPUT[2]);
  and and_8 (and_8_out, and_1_out, not_3_out);
  and and_9 (and_9_out, and_1_out, INPUT[3]);
  and and_10 (and_10_out, and_1_out, not_4_out);
  and and_11 (and_11_out, and_1_out, INPUT[4]);
  and and_12 (and_12_out, and_1_out, not_5_out);
  and and_13 (and_13_out, and_1_out, INPUT[5]);
  and and_14 (and_14_out, and_1_out, not_6_out);
  and and_15 (and_15_out, and_1_out, INPUT[6]);
  and and_16 (and_16_out, and_1_out, not_7_out);
  and and_17 (and_17_out, and_2_out, OUTPUT[0]);
  and and_18 (and_18_out, and_17_out, OUTPUT[1]);
  and and_19 (and_19_out, and_18_out, OUTPUT[2]);
  and and_20 (and_20_out, and_19_out, OUTPUT[3]);
  and and_21 (and_21_out, and_20_out, OUTPUT[4]);
  and and_22 (and_22_out, and_21_out, OUTPUT[5]);
  or or_1 (or_1_out, and_2_out, and_2_out, and_3_out);
  or or_2 (or_2_out, and_2_out, and_2_out, and_4_out);
  or or_3 (or_3_out, and_17_out, and_17_out, and_5_out);
  or or_4 (or_4_out, and_17_out, and_17_out, and_6_out);
  or or_5 (or_5_out, and_18_out, and_18_out, and_7_out);
  or or_6 (or_6_out, and_18_out, and_18_out, and_8_out);
  or or_7 (or_7_out, and_19_out, and_19_out, and_9_out);
  or or_8 (or_8_out, and_19_out, and_19_out, and_10_out);
  or or_9 (or_9_out, and_11_out, and_20_out, and_11_out);
  or or_10 (or_10_out, and_20_out, and_20_out, and_12_out);
  or or_11 (or_11_out, and_21_out, and_21_out, and_13_out);
  or or_12 (or_12_out, and_21_out, and_21_out, and_14_out);
  or or_13 (or_13_out, and_22_out, and_22_out, and_15_out);
  or or_14 (or_14_out, and_22_out, and_22_out, and_16_out);
  J_K_Flip_Flop j_k_ff_1 (.J(or_1_out), .clk(CLK), .K(or_2_out), .Q(OUTPUT[0]), .reset(CLR));  // open: Qn, preset, en
  J_K_Flip_Flop j_k_ff_2 (.J(or_3_out), .clk(CLK), .K(or_4_out), .Q(OUTPUT[1]), .reset(CLR));  // open: Qn, preset, en
  J_K_Flip_Flop j_k_ff_3 (.J(or_5_out), .clk(CLK), .K(or_6_out), .Q(OUTPUT[2]), .reset(CLR));  // open: Qn, preset, en
  J_K_Flip_Flop j_k_ff_4 (.J(or_7_out), .clk(CLK), .K(or_8_out), .Q(OUTPUT[3]), .reset(CLR));  // open: Qn, preset, en
  J_K_Flip_Flop j_k_ff_5 (.J(or_9_out), .clk(CLK), .K(or_10_out), .Q(OUTPUT[4]), .reset(CLR));  // open: Qn, preset, en
  J_K_Flip_Flop j_k_ff_6 (.J(or_11_out), .clk(CLK), .K(or_12_out), .Q(OUTPUT[5]), .reset(CLR));  // open: Qn, preset, en
  J_K_Flip_Flop j_k_ff_7 (.J(or_13_out), .clk(CLK), .K(or_14_out), .Q(OUTPUT[6]), .reset(CLR));  // open: Qn, preset, en
endmodule
