// Logisim project 7bit increamenter.circ as structural Verilog: 1 circuit, main circuit main
module main (
  input  [6:0] INPUT,
  output [6:0] OUTPUT
);

  wire main_1_c, main_2_c, main_3_c, main_4_c, main_5_c, main_6_c;

  HA_main main_1 (.A(1'b1), .B(INPUT[0]), .S(OUTPUT[0]), .C(main_1_c));
  HA_main main_2 (.A(main_1_c), .B(INPUT[1]), .S(OUTPUT[1]), .C(main_2_c));
  HA_main main_3 (.A(main_2_c), .B(INPUT[2]), .S(OUTPUT[2]), .C(main_3_c));
  HA_main main_4 (.A(main_3_c), .B(INPUT[3]), .S(OUTPUT[3]), .C(main_4_c));
  HA_main main_5 (.A(main_4_c), .B(INPUT[4]), .S(OUTPUT[4]), .C(main_5_c));
  HA_main main_6 (.A(main_5_c), .B(INPUT[5]), .S(OUTPUT[5]), .C(main_6_c));
  HA_main main_7 (.A(main_6_c), .B(INPUT[6]), .S(OUTPUT[6]));  // open: C

  // Notes on the sheet:
  //   7 BIT INCREMENTER
  //   HA
  //   HA
  //   HA
  //   HA
  //   HA
  //   HA
  //   HA
endmodule
