// Logisim project ALU 1 BIT.circ as structural Verilog: 1 circuit, main circuit main
module main (
  input  ADD,
  input  DRTAC,
  input  SUB,
  input  OR,
  input  AND,
  input  XOR,
  input  COM,
  input  SHL,
  input  SHR,
  input  B_IN,
  input  prev_in,
  input  LD,
  input  AC0,
  input  DR_i,
  input  AC_i_1,
  input  AC_i_1_2,
  output cout,
  output B_OUT,
  output AC_OUT
);

  wire adder_1_out, and_1_out, and_2_out, and_3_out, and_4_out, and_5_out, and_6_out, and_7_out, and_8_out,
       and_9_out, not_1_out, or_1_out, or_2_out, subtractor_1_out, xor_1_out;

  not not_1 (not_1_out, AC0);
  Adder #(.width(1)) adder_1 (.a(AC0), .b(DR_i), .out(adder_1_out), .cin(prev_in), .cout(cout));
  Subtractor #(.width(1)) subtractor_1 (.a(AC0), .b(DR_i), .out(subtractor_1_out), .bin(B_IN), .bout(B_OUT));
  or or_1 (or_1_out, AC0, DR_i);
  xor xor_1 (xor_1_out, AC0, DR_i);
  and and_1 (and_1_out, ADD, adder_1_out);
  and and_2 (and_2_out, DRTAC, DR_i);
  and and_3 (and_3_out, SUB, subtractor_1_out);
  and and_4 (and_4_out, OR, or_1_out);
  and and_5 (and_5_out, AND, AC0, DR_i);
  and and_6 (and_6_out, XOR, xor_1_out);
  and and_7 (and_7_out, not_1_out, COM);
  and and_8 (and_8_out, SHL, AC_i_1);
  and and_9 (and_9_out, SHR, AC_i_1_2);
  or or_2 (or_2_out, and_1_out, and_2_out, and_3_out, and_4_out, and_5_out, and_6_out, and_7_out, and_8_out, and_9_out);
  and and_10 (AC_OUT, LD, or_2_out);
endmodule
