// Logisim project ALU 16 BIT.circ as structural Verilog: 1 circuit, main circuit main
module main (
  input  ADD,
  input  DRTAC,
  input  SUB,
  input  OR,
  input  AND,
  input  XOR,
  input  COM,
  input  SHL,
  input  SHR,
  input  [15:0] AC_IN,
  input  LD,
  input  [15:0] DR_IN,
  input  clock_for_E,
  output [15:0] AC_OUT,
  output E_carry
);

  wire and_1_out, and_2_out, main_1_b_out, main_1_carry, main_2_b_out, main_2_carry, or_1_out;

  ALU_8_BIT_main main_1 (
    .AC0(AC_IN[0]), .AC1(AC_IN[1]), .AC2(AC_IN[2]), .AC3(AC_IN[3]), .AC4(AC_IN[4]), .AC5(AC_IN[5]),
    .AC6(AC_IN[6]), .AC7(AC_IN[7]), .DR0(DR_IN[0]), .DR1(DR_IN[1]), .DR2(DR_IN[2]), .DR3(DR_IN[3]),
    .DR4(DR_IN[4]), .DR5(DR_IN[5]), .DR6(DR_IN[6]), .DR7(DR_IN[7]), .ADD(ADD), .DRTAC(DRTAC), .SUB(SUB),
    .OR(OR), .AND(AND), .XOR(XOR), .COM(COM), .SHL(SHL), .SHR(SHR), .E(E_carry), .B_IN(1'b0), .PREV_IN(1'b0),
    .AC_i_1(AC_IN[8]), .B_out(main_1_b_out), .carry(main_1_carry), .LD(LD), .AC0_OUT(AC_OUT[0]),
    .AC1_OUT(AC_OUT[1]), .AC2_OUT(AC_OUT[2]), .AC3_OUT(AC_OUT[3]), .AC4_OUT(AC_OUT[4]), .AC5_OUT(AC_OUT[5]),
    .AC6_OUT(AC_OUT[6]), .AC7_OUT(AC_OUT[7]));
  and and_1 (and_1_out, SHL, AC_IN[15]);
  and and_2 (and_2_out, SHR, AC_IN[0]);
  or or_1 (or_1_out, main_2_carry, main_2_b_out, and_1_out, and_2_out);
  ALU_8_BIT_main main_2 (
    .AC0(AC_IN[8]), .AC1(AC_IN[9]), .AC2(AC_IN[10]), .AC3(AC_IN[11]), .AC4(AC_IN[12]), .AC5(AC_IN[13]),
    .AC6(AC_IN[14]), .AC7(AC_IN[15]), .DR0(DR_IN[8]), .DR1(DR_IN[9]), .DR2(DR_IN[10]), .DR3(DR_IN[11]),
    .DR4(DR_IN[12]), .DR5(DR_IN[13]), .DR6(DR_IN[14]), .DR7(DR_IN[15]), .ADD(ADD), .DRTAC(DRTAC), .SUB(SUB),
    .OR(OR), .AND(AND), .XOR(XOR), .COM(COM), .SHL(SHL), .SHR(SHR), .E(AC_IN[7]), .B_IN(main_1_b_out),
    .PREV_IN(main_1_carry), .AC_i_1(E_carry), .B_out(main_2_b_out), .carry(main_2_carry), .LD(LD),
    .AC0_OUT(AC_OUT[8]), .AC1_OUT(AC_OUT[9]), .AC2_OUT(AC_OUT[10]), .AC3_OUT(AC_OUT[11]),
    .AC4_OUT(AC_OUT[12]), .AC5_OUT(AC_OUT[13]), .AC6_OUT(AC_OUT[14]), .AC7_OUT(AC_OUT[15]));
  D_Flip_Flop d_ff_1 (.clk(clock_for_E), .D(or_1_out), .Q(E_carry));  // open: Qn, preset, en, reset
endmodule
