// Logisim project ALU 2 BIT.circ as structural Verilog: 1 circuit, main circuit main
module main (
  input  ADD,
  input  DRTAC,
  input  SUB,
  input  OR,
  input  AND,
  input  XOR,
  input  COM,
  input  SHL,
  input  SHR,
  input  AC0,
  input  AC1,
  input  DR0,
  input  DR1,
  input  PREV_IN,
  input  LD,
  input  B_IN,
  input  E_ACi_1,
  input  AC_i_1,
  output AC0_OUT,
  output AC1_OUT,
  output B_OUT,
  output COUT
);

  wire main_1_b_out, main_1_cout;

  ALU_1_BIT_main main_1 (
    .B_IN(B_IN), .prev_in(PREV_IN), .AC0(AC0), .DR_i(DR0), .AC_i_1(E_ACi_1), .AC_i_1_2(AC1), .ADD(ADD),
    .DRTAC(DRTAC), .SUB(SUB), .OR(OR), .AND(AND), .XOR(XOR), .COM(COM), .SHL(SHL), .SHR(SHR),
    .B_OUT(main_1_b_out), .cout(main_1_cout), .LD(LD), .AC_OUT(AC0_OUT));
  ALU_1_BIT_main main_2 (
    .B_IN(main_1_b_out), .prev_in(main_1_cout), .AC0(AC1), .DR_i(DR1), .AC_i_1(AC0), .AC_i_1_2(AC_i_1),
    .ADD(ADD), .DRTAC(DRTAC), .SUB(SUB), .OR(OR), .AND(AND), .XOR(XOR), .COM(COM), .SHL(SHL), .SHR(SHR),
    .B_OUT(B_OUT), .cout(COUT), .LD(LD), .AC_OUT(AC1_OUT));
endmodule
