// Logisim project ALU 8 BIT.circ as structural Verilog: 1 circuit, main circuit main
module main (
  input  ADD,
  input  DRTAC,
  input  SUB,
  input  OR,
  input  AND,
  input  XOR,
  input  COM,
  input  SHL,
  input  SHR,
  input  AC0,
  input  AC1,
  input  AC2,
  input  AC3,
  input  AC4,
  input  AC5,
  input  AC6,
  input  AC7,
  input  DR0,
  input  DR1,
  input  LD,
  input  DR2,
  input  DR3,
  input  DR4,
  input  DR5,
  input  DR6,
  input  DR7,
  input  E,
  input  B_IN,
  input  PREV_IN,
  input  AC_i_1,
  output AC0_OUT,
  output AC1_OUT,
  output AC2_OUT,
  output AC3_OUT,
  output AC4_OUT,
  output AC5_OUT,
  output AC6_OUT,
  output AC7_OUT,
  output B_out,
  output carry
);

  wire main_1_b_out, main_1_cout, main_2_b_out, main_2_cout, main_3_b_out, main_3_cout;

  ALU_2_BIT_main main_1 (
    .AC0(AC0), .AC1(AC1), .DR0(DR0), .DR1(DR1), .ADD(ADD), .DRTAC(DRTAC), .SUB(SUB), .OR(OR), .AND(AND),
    .XOR(XOR), .COM(COM), .SHL(SHL), .SHR(SHR), .E_ACi_1(E), .B_IN(B_IN), .PREV_IN(PREV_IN), .AC_i_1(AC2),
    .B_OUT(main_1_b_out), .COUT(main_1_cout), .AC0_OUT(AC0_OUT), .AC1_OUT(AC1_OUT), .LD(LD));
  ALU_2_BIT_main main_2 (
    .AC0(AC2), .AC1(AC3), .DR0(DR2), .DR1(DR3), .ADD(ADD), .DRTAC(DRTAC), .SUB(SUB), .OR(OR), .AND(AND),
    .XOR(XOR), .COM(COM), .SHL(SHL), .SHR(SHR), .E_ACi_1(AC1), .B_IN(main_1_b_out), .PREV_IN(main_1_cout),
    .AC_i_1(AC4), .B_OUT(main_2_b_out), .COUT(main_2_cout), .AC0_OUT(AC2_OUT), .AC1_OUT(AC3_OUT), .LD(LD));
  ALU_2_BIT_main main_3 (
    .AC0(AC4), .AC1(AC5), .DR0(DR4), .DR1(DR5), .ADD(ADD), .DRTAC(DRTAC), .SUB(SUB), .OR(OR), .AND(AND),
    .XOR(XOR), .COM(COM), .SHL(SHL), .SHR(SHR), .E_ACi_1(AC3), .B_IN(main_2_b_out), .PREV_IN(main_2_cout),
    .AC_i_1(AC6), .B_OUT(main_3_b_out), .COUT(main_3_cout), .AC0_OUT(AC4_OUT), .AC1_OUT(AC5_OUT), .LD(LD));
  ALU_2_BIT_main main_4 (
    .AC0(AC6), .AC1(AC7), .DR0(DR6), .DR1(DR7), .ADD(ADD), .DRTAC(DRTAC), .SUB(SUB), .OR(OR), .AND(AND),
    .XOR(XOR), .COM(COM), .SHL(SHL), .SHR(SHR), .E_ACi_1(AC5), .B_IN(main_3_b_out), .PREV_IN(main_3_cout),
    .AC_i_1(AC_i_1), .B_OUT(B_out), .COUT(carry), .AC0_OUT(AC6_OUT), .AC1_OUT(AC7_OUT), .LD(LD));
endmodule
