// Logisim project ALU 1 Bit.circ as structural Verilog: 1 circuit, main circuit main
module main (
  input  AND,
  input  ADD,
  input  DR,
  input  INP,
  input  COM,
  input  SHR,
  input  SHL,
  input  LD,
  input  AC0,
  input  DR_i,
  input  previous_in,
  input  inpr_i,
  input  AC_i_1,
  input  AC_i_1_2,
  output cout,
  output Output
);

  wire adder_1_out, and_1_out, and_2_out, and_3_out, and_4_out, and_5_out, and_6_out, and_7_out, not_1_out,
       or_1_out;

  Adder #(.width(1)) adder_1 (.a(AC0), .b(DR_i), .out(adder_1_out), .cin(previous_in), .cout(cout));
  and and_1 (and_1_out, AND, AC0, DR_i);
  and and_2 (and_2_out, ADD, adder_1_out);
  and and_3 (and_3_out, DR_i, DR);
  and and_4 (and_4_out, INP, inpr_i);
  not not_1 (not_1_out, AC0);
  and and_5 (and_5_out, not_1_out, COM);
  and and_6 (and_6_out, AC_i_1, SHR);
  and and_7 (and_7_out, SHL, AC_i_1_2);
  or or_1 (or_1_out, and_1_out, and_2_out, and_3_out, and_4_out, and_5_out, and_6_out, and_7_out);
  and and_8 (Output, LD, or_1_out);
endmodule
