// Logisim project NEW 8 BIT.circ as structural Verilog: 1 circuit, main circuit main
module main (
  input  AND,
  input  ADD,
  input  DR,
  input  INP,
  input  COMP,
  input  SHR,
  input  SHL,
  input  AC0_IN,
  input  AC1_IN,
  input  AC2_IN,
  input  AC3_IN,
  input  AC4_IN,
  input  AC5_IN,
  input  AC6_IN,
  input  AC7_IN,
  input  DR0,
  input  DR1,
  input  LD,
  input  DR2,
  input  DR3,
  input  DR4,
  input  DR5,
  input  DR6,
  input  DR7,
  input  AC_I_1,
  input  INPR0,
  input  INPR1,
  input  INPR2,
  input  PREV_IN,
  input  INPR3,
  input  INPR4,
  input  INPR5,
  input  INPR6,
  input  E,
  input  INPR7,
  output AC0_OUT,
  output AC1_OUT,
  output AC2_OUT,
  output AC3_OUT,
  output AC4_OUT,
  output AC5_OUT,
  output AC6_OUT,
  output AC7_OUT,
  output CARRY
);

  wire main_1_cout, main_2_cout, main_3_cout;

  NEW_ALU_2_BIT_main main_1 (
    .AC0_IN(AC0_IN), .AC1_IN(AC1_IN), .DR0_IN(DR0), .DR1_IN(DR1), .INPR0(INPR0), .INPR1(INPR1), .AND(AND),
    .ADD(ADD), .DR(DR), .INP(INP), .COMP(COMP), .SHR(SHR), .SHL(SHL), .E(E), .PREVIOUS_IN(PREV_IN),
    .ACI_1(AC2_IN), .cout(main_1_cout), .AC0_OUT(AC0_OUT), .AC1_OUT(AC1_OUT), .LD(LD));
  NEW_ALU_2_BIT_main main_2 (
    .AC0_IN(AC2_IN), .AC1_IN(AC3_IN), .DR0_IN(DR2), .DR1_IN(DR3), .INPR0(INPR2), .INPR1(INPR3), .AND(AND),
    .ADD(ADD), .DR(DR), .INP(INP), .COMP(COMP), .SHR(SHR), .SHL(SHL), .E(AC1_IN), .PREVIOUS_IN(main_1_cout),
    .ACI_1(AC4_IN), .cout(main_2_cout), .AC0_OUT(AC2_OUT), .AC1_OUT(AC3_OUT), .LD(LD));
  NEW_ALU_2_BIT_main main_3 (
    .AC0_IN(AC4_IN), .AC1_IN(AC5_IN), .DR0_IN(DR4), .DR1_IN(DR5), .INPR0(INPR4), .INPR1(INPR5), .AND(AND),
    .ADD(ADD), .DR(DR), .INP(INP), .COMP(COMP), .SHR(SHR), .SHL(SHL), .E(AC2_IN), .PREVIOUS_IN(main_2_cout),
    .ACI_1(AC6_IN), .cout(main_3_cout), .AC0_OUT(AC4_OUT), .AC1_OUT(AC5_OUT), .LD(LD));
  NEW_ALU_2_BIT_main main_4 (
    .AC0_IN(AC6_IN), .AC1_IN(AC7_IN), .DR0_IN(DR6), .DR1_IN(DR7), .INPR0(INPR6), .INPR1(INPR7), .AND(AND),
    .ADD(ADD), .DR(DR), .INP(INP), .COMP(COMP), .SHR(SHR), .SHL(SHL), .E(AC5_IN), .PREVIOUS_IN(main_3_cout),
    .ACI_1(AC_I_1), .cout(CARRY), .AC0_OUT(AC6_OUT), .AC1_OUT(AC7_OUT), .LD(LD));
endmodule
