// Logisim project NEW ALU 16 BIT ver1.circ as structural Verilog: 1 circuit, main circuit main
module main (
  input  AND,
  input  ADD,
  input  DR,
  input  IN,
  input  COMP,
  input  SHR,
  input  SHL,
  input  [15:0] AC_IN,
  input  LD,
  input  [15:0] DR_IN,
  input  [7:0] INPR,
  input  clock_for_E,
  output [15:0] ac_out,
  output E_carry
);

  wire and_1_out, and_2_out, main_1_carry, main_2_carry, or_1_out, undriven;

  NEW_8_BIT_main main_1 (
    .AC0_IN(AC_IN[0]), .AC1_IN(AC_IN[1]), .AC2_IN(AC_IN[2]), .AC3_IN(AC_IN[3]), .AC4_IN(AC_IN[4]),
    .AC5_IN(AC_IN[5]), .AC6_IN(AC_IN[6]), .AC7_IN(AC_IN[7]), .DR0(DR_IN[0]), .DR1(DR_IN[1]), .DR2(DR_IN[2]),
    .DR3(DR_IN[3]), .DR4(DR_IN[4]), .DR5(DR_IN[5]), .DR6(DR_IN[6]), .DR7(DR_IN[7]), .AND(AND), .ADD(ADD),
    .DR(DR), .INP(IN), .COMP(COMP), .SHR(SHR), .SHL(SHL), .INPR0(INPR[7]), .INPR1(INPR[6]), .INPR2(INPR[5]),
    .INPR3(INPR[4]), .INPR4(INPR[3]), .INPR5(INPR[2]), .INPR6(INPR[1]), .INPR7(INPR[0]), .E(E_carry),
    .PREV_IN(1'b0), .AC_I_1(AC_IN[8]), .CARRY(main_1_carry), .LD(LD), .AC0_OUT(ac_out[0]),
    .AC1_OUT(ac_out[1]), .AC2_OUT(ac_out[2]), .AC3_OUT(ac_out[3]), .AC4_OUT(ac_out[4]), .AC5_OUT(ac_out[5]),
    .AC6_OUT(ac_out[6]), .AC7_OUT(ac_out[7]));
  and and_1 (and_1_out, AC_IN[15], SHL);
  and and_2 (and_2_out, SHR, AC_IN[0]);
  or or_1 (or_1_out, and_1_out, main_2_carry, and_2_out);
  NEW_8_BIT_main main_2 (
    .AC0_IN(AC_IN[8]), .AC1_IN(AC_IN[9]), .AC2_IN(AC_IN[10]), .AC3_IN(AC_IN[11]), .AC4_IN(AC_IN[12]),
    .AC5_IN(AC_IN[13]), .AC6_IN(AC_IN[14]), .AC7_IN(AC_IN[15]), .DR0(DR_IN[8]), .DR1(DR_IN[9]),
    .DR2(DR_IN[10]), .DR3(DR_IN[11]), .DR4(DR_IN[12]), .DR5(DR_IN[13]), .DR6(DR_IN[14]), .DR7(DR_IN[15]),
    .AND(AND), .ADD(ADD), .DR(DR), .INP(IN), .COMP(COMP), .SHR(SHR), .SHL(SHL), .INPR0(1'b0), .INPR1(1'b0),
    .INPR2(1'b0), .INPR3(1'b0), .INPR4(1'b0), .INPR5(1'b0), .INPR6(1'b0), .INPR7(1'b0), .E(AC_IN[7]),
    .PREV_IN(main_1_carry), .AC_I_1(E_carry), .CARRY(main_2_carry), .LD(LD), .AC0_OUT(ac_out[8]),
    .AC1_OUT(ac_out[9]), .AC2_OUT(ac_out[10]), .AC3_OUT(ac_out[11]), .AC4_OUT(ac_out[12]),
    .AC5_OUT(ac_out[13]), .AC6_OUT(ac_out[14]), .AC7_OUT(ac_out[15]));
  D_Flip_Flop d_ff_1 (.clk(clock_for_E), .D(or_1_out), .Q(E_carry), .reset(undriven));  // open: Qn, preset, en
endmodule
