// Logisim project NEW ALU 2 BIT.circ as structural Verilog: 1 circuit, main circuit main
module main (
  input  COMP,
  input  SHR,
  input  SHL,
  input  DR,
  input  INP,
  input  ADD,
  input  AND,
  input  AC0_IN,
  input  AC1_IN,
  input  DR0_IN,
  input  DR1_IN,
  input  PREVIOUS_IN,
  input  INPR0,
  input  INPR1,
  input  LD,
  input  E,
  input  ACI_1,
  output AC0_OUT,
  output AC1_OUT,
  output cout
);

  wire main_1_cout;

  ALU_1_Bit_main main_1 (
    .AC0(AC0_IN), .DR_i(DR0_IN), .previous_in(PREVIOUS_IN), .inpr_i(INPR0), .AC_i_1(AC1_IN), .AC_i_1_2(E),
    .AND(AND), .ADD(ADD), .DR(DR), .INP(INP), .COM(COMP), .SHR(SHR), .SHL(SHL), .cout(main_1_cout), .LD(LD),
    .Output(AC0_OUT));
  ALU_1_Bit_main main_2 (
    .AC0(AC1_IN), .DR_i(DR1_IN), .previous_in(main_1_cout), .inpr_i(INPR1), .AC_i_1(ACI_1),
    .AC_i_1_2(AC0_IN), .AND(AND), .ADD(ADD), .DR(DR), .INP(INP), .COM(COMP), .SHR(SHR), .SHL(SHL),
    .cout(cout), .LD(LD), .Output(AC1_OUT));
endmodule
