// Logisim project Sequence Logic.circ as structural Verilog: 1 circuit, main circuit main
module main (
  input  I1,
  input  I0,
  input  T,
  output LDSBR,
  output S1,
  output S0
);

  wire and_2_out, and_3_out, not_1_out;

  not not_1 (not_1_out, I1);
  and and_1 (LDSBR, not_1_out, I0, T);
  and and_2 (and_2_out, I0, I1);
  or or_1 (S0, and_2_out, and_3_out);
  and and_3 (and_3_out, not_1_out, T);

  assign S1 = I1;
endmodule
