// Logisim project FINAL BUS CONTROL.circ as structural Verilog: 1 circuit, main circuit main
module main (
  input  [6:0] D0_D6,
  input  D7_prime,
  input  T0,
  input  T1,
  input  T2,
  input  T3,
  input  T4,
  input  T5,
  input  T6,
  input  R,
  input  R_prime,
  input  I,
  input  p,
  input  B10,
  output S2,
  output S1,
  output S0
);

  wire and_1_out, and_2_out, and_3_out, and_4_out, and_5_out, and_6_out, and_7_out, and_8_out, and_9_out,
       and_10_out, and_11_out, and_12_out, and_13_out, and_14_out, or_1_out, or_2_out, or_3_out, or_4_out,
       or_5_out, or_6_out;

  and and_1 (and_1_out, D0_D6[4], T4);
  and and_2 (and_2_out, D0_D6[5], T5);
  and and_3 (and_3_out, R_prime, T0);
  and and_4 (and_4_out, R, T0);
  and and_5 (and_5_out, D0_D6[5], T4);
  and and_6 (and_6_out, D0_D6[2], T5);
  and and_7 (and_7_out, T6, D0_D6[6]);
  and and_8 (and_8_out, T4, D0_D6[3]);
  and and_9 (and_9_out, R_prime, T2);
  and and_10 (and_10_out, R, T1);
  and and_11 (and_11_out, p, B10);
  or or_1 (or_1_out, D0_D6[0], D0_D6[1], D0_D6[2], D0_D6[6]);
  or or_2 (or_2_out, and_1_out, and_2_out);
  or or_3 (or_3_out, and_3_out, and_4_out, and_5_out);
  or or_4 (or_4_out, and_6_out, and_7_out);
  or or_5 (or_5_out, and_11_out, and_8_out);
  and and_12 (and_12_out, or_1_out, T4);
  and and_13 (and_13_out, D7_prime, I, T3);
  and and_14 (and_14_out, R_prime, T1);
  or or_6 (or_6_out, and_12_out, and_13_out, and_14_out);
  encoder_for_bus_main main_1 (
    .X1(or_2_out), .X2(or_3_out), .X3(or_4_out), .X4(or_5_out), .X5(and_9_out), .X6(and_10_out),
    .X7(or_6_out), .S2(S2), .S1(S1), .S0(S0));
endmodule
