// Logisim project bus line new.circ as structural Verilog: 1 circuit, main circuit main
module main (
  input  [11:0] _001,
  input  [2:0] selection,
  input  [11:0] _010,
  input  [15:0] _011,
  input  [15:0] _100,
  input  [15:0] _101,
  input  [15:0] _110,
  input  [15:0] _111,
  output [15:0] \output 
);

  wire [15:12] undriven, undriven_2;

  Multiplexer #(.select(3), .width(16)) multiplexer_1 (
    .in0({16{1'b0}}), .in1({undriven_2, _001}), .in2({undriven, _010}), .in3(_011), .in4(_100), .in5(_101),
    .in6(_110), .in7(_111), .out(\output ), .sel(selection));  // open: en
endmodule
