// Logisim project x1 x7 control.circ as structural Verilog: 1 circuit, main circuit main
module main (
  input  [6:0] D0_D6,
  input  D7_prime,
  input  T0,
  input  T1,
  input  T2,
  input  T3,
  input  T4,
  input  T5,
  input  T6,
  input  R,
  input  R_prime,
  input  I,
  input  p,
  input  B10,
  output X1,
  output X2,
  output X3,
  output X4,
  output X5,
  output X6,
  output X7
);

  wire and_1_out, and_2_out, and_3_out, and_4_out, and_5_out, and_6_out, and_7_out, and_8_out, and_11_out,
       and_12_out, and_13_out, and_14_out, or_1_out;

  and and_1 (and_1_out, D0_D6[4], T4);
  and and_2 (and_2_out, D0_D6[5], T5);
  and and_3 (and_3_out, R_prime, T0);
  and and_4 (and_4_out, R, T0);
  and and_5 (and_5_out, D0_D6[5], T4);
  and and_6 (and_6_out, D0_D6[2], T5);
  and and_7 (and_7_out, T6, D0_D6[6]);
  and and_8 (and_8_out, T4, D0_D6[3]);
  and and_9 (X5, R_prime, T2);
  and and_10 (X6, R, T1);
  and and_11 (and_11_out, p, B10);
  or or_1 (or_1_out, D0_D6[0], D0_D6[1], D0_D6[2], D0_D6[6]);
  or or_2 (X1, and_1_out, and_2_out);
  or or_3 (X2, and_3_out, and_4_out, and_5_out);
  or or_4 (X3, and_6_out, and_7_out);
  or or_5 (X4, and_11_out, and_8_out);
  and and_12 (and_12_out, or_1_out, T4);
  and and_13 (and_13_out, D7_prime, I, T3);
  and and_14 (and_14_out, R_prime, T1);
  or or_6 (X7, and_12_out, and_13_out, and_14_out);
endmodule
