// Logisim project AC control.circ as structural Verilog: 1 circuit, main circuit main
module main (
  input  D0,
  input  T5,
  input  D1,
  input  D2,
  input  T5_2,
  input  P,
  input  B11,
  input  r,
  input  B9,
  input  B7,
  input  B6,
  input  B5,
  input  B11_2,
  output AND,
  output ADD,
  output DR,
  output INPR,
  output COM,
  output LD,
  output SHR,
  output SHL,
  output INR,
  output CLR
);

  and and_1 (AND, D0, T5);
  and and_2 (ADD, D1, T5);
  and and_3 (DR, D2, T5_2);
  and and_4 (INPR, P, B11);
  and and_5 (COM, r, B9);
  and and_6 (SHR, r, B7);
  and and_7 (SHL, r, B6);
  and and_8 (INR, r, B5);
  and and_9 (CLR, r, B11_2);
  or or_1 (LD, AND, ADD, DR, INPR, COM, SHR, SHL);
endmodule
