// Logisim project AR control.circ as structural Verilog: 1 circuit, main circuit main
module main (
  input  D_prime_7,
  input  I,
  input  T3,
  input  T2,
  input  R,
  input  T0,
  input  D5,
  input  T4,
  output LD,
  output INR,
  output CLR
);

  wire and_1_out, and_2_out, and_3_out, not_1_out;

  not not_1 (not_1_out, R);
  and and_1 (and_1_out, D_prime_7, I, T3);
  and and_2 (and_2_out, T2, not_1_out);
  and and_3 (and_3_out, not_1_out, T0);
  and and_4 (INR, D5, T4);
  and and_5 (CLR, T0, R);
  or or_1 (LD, and_1_out, and_2_out, and_3_out);
endmodule
