// Logisim project DR control.circ as structural Verilog: 1 circuit, main circuit main
module main (
  input  D0,
  input  T4,
  input  D1,
  input  D2,
  input  D6,
  input  T5,
  output LD,
  output INR
);

  wire and_1_out, and_2_out, and_3_out, and_4_out;

  and and_1 (and_1_out, D0, T4);
  and and_2 (and_2_out, D1, T4);
  and and_3 (and_3_out, D2, T4);
  and and_4 (and_4_out, D6, T4);
  and and_5 (INR, D6, T5);
  or or_1 (LD, and_1_out, and_2_out, and_3_out, and_4_out);
endmodule
