// Logisim project E CLR COM.circ as structural Verilog: 1 circuit, main circuit main
module main (
  input  r,
  input  B10,
  input  B8,
  output CLR,
  output COM
);

  and and_1 (CLR, r, B10);

  assign COM = B8;
endmodule
