// Logisim project IEN control.circ as structural Verilog: 1 circuit, main circuit main
module main (
  input  Clock,
  input  p,
  input  B7,
  input  B6,
  input  R,
  input  T2,
  output IEN
);

  wire and_1_out, and_2_out, and_3_out, or_1_out;

  and and_1 (and_1_out, p, B7);
  and and_2 (and_2_out, p, B6);
  and and_3 (and_3_out, R, T2);
  or or_1 (or_1_out, and_2_out, and_3_out);
  J_K_Flip_Flop j_k_ff_1 (.J(and_1_out), .clk(Clock), .K(or_1_out), .Q(IEN));  // open: Qn, preset, en, reset
endmodule
