// Logisim project IR with decoder.circ as structural Verilog: 1 circuit, main circuit main
module main (
  input  [15:0] IR,
  output D0,
  output D1,
  output D2,
  output D3,
  output D4,
  output D5,
  output D6,
  output D7,
  output [11:0] AR,
  output I
);

  Decoder #(.select(3), .enable("false")) decoder_1 (
    .out0(D0), .out1(D1), .out2(D2), .out3(D3), .out4(D4), .out5(D5), .out6(D6), .out7(D7), .sel(IR[14:12]));

  assign AR = IR[11:0];
  assign I = IR[15];
endmodule
