// Logisim project PC control.circ as structural Verilog: 1 circuit, main circuit main
module main (
  input  D4,
  input  T4,
  input  D5,
  input  T5,
  input  R_prime,
  input  T1,
  input  R,
  input  T2,
  input  D6,
  input  T6,
  input  r_2,
  input  B4,
  input  B3,
  input  B2,
  input  B1,
  input  P,
  input  B9,
  input  B8,
  input  R_3,
  input  T1_2,
  output LD,
  output INR,
  output CLR
);

  wire and_1_out, and_2_out, and_3_out, and_4_out, and_5_out, and_6_out, and_7_out, and_8_out, and_9_out,
       and_10_out, and_11_out;

  and and_1 (and_1_out, D4, T4);
  and and_2 (and_2_out, D5, T5);
  and and_3 (and_3_out, R_prime, T1);
  and and_4 (and_4_out, R, T2);
  and and_5 (and_5_out, D6, T6);
  and and_6 (and_6_out, r_2, B4);
  and and_7 (and_7_out, r_2, B3);
  and and_8 (and_8_out, r_2, B2);
  and and_9 (and_9_out, r_2, B1);
  and and_10 (and_10_out, P, B9);
  and and_11 (and_11_out, P, B8);
  and and_12 (CLR, R_3, T1_2);
  or or_1 (LD, and_1_out, and_2_out);
  or or_2 (INR, and_3_out, and_4_out, and_5_out, and_6_out, and_7_out, and_8_out, and_9_out, and_10_out, and_11_out);
endmodule
