// Logisim project TR control.circ as structural Verilog: 1 circuit, main circuit main
module main (
  input  RCOMP,
  input  T1,
  output LD
);

  wire not_1_out;

  not not_1 (not_1_out, RCOMP);
  and and_1 (LD, not_1_out, T1);
endmodule
