// Logisim project memory control.circ as structural Verilog: 1 circuit, main circuit main
module main (
  input  D0,
  input  D1,
  input  D2,
  input  D3,
  input  D4,
  input  D5,
  input  D6,
  input  D7,
  input  I,
  input  R,
  input  T1,
  input  T4,
  input  T3,
  input  T6,
  output Write,
  output Read
);

  wire and_1_out, and_2_out, and_3_out, and_4_out, and_5_out, and_6_out, and_7_out, and_8_out, and_9_out,
       and_10_out, not_1_out, not_2_out;

  not not_1 (not_1_out, D7);
  not not_2 (not_2_out, R);
  and and_1 (and_1_out, R, T1);
  and and_2 (and_2_out, D3, T4);
  and and_3 (and_3_out, D5, T4);
  and and_4 (and_4_out, D6, T6);
  and and_5 (and_5_out, not_2_out, T1);
  and and_6 (and_6_out, not_1_out, I, T3);
  and and_7 (and_7_out, D0, T4);
  and and_8 (and_8_out, D1, T4);
  and and_9 (and_9_out, D2, T4);
  and and_10 (and_10_out, D6, T4);
  or or_1 (Write, and_1_out, and_2_out, and_3_out, and_4_out);
  or or_2 (Read, and_5_out, and_6_out, and_7_out, and_8_out, and_9_out, and_10_out);
endmodule
