// Logisim project r control.circ as structural Verilog: 1 circuit, main circuit main
module main (
  input  T0,
  input  T1,
  input  T2,
  input  IEN,
  input  FGI,
  input  FGO,
  input  R,
  input  Clock,
  output R_2
);

  wire and_1_out, and_2_out, not_1_out, not_2_out, not_3_out, or_1_out;

  not not_1 (not_1_out, T1);
  not not_2 (not_2_out, T2);
  or or_1 (or_1_out, FGI, FGO);
  not not_3 (not_3_out, T0);
  and and_1 (and_1_out, not_3_out, not_1_out, not_2_out, IEN, or_1_out);
  and and_2 (and_2_out, T2, R);
  J_K_Flip_Flop j_k_ff_1 (.J(and_1_out), .clk(Clock), .K(and_2_out), .Q(R_2));  // open: Qn, preset, en, reset
endmodule
