// Logisim project comp1.circ as structural Verilog: 1 circuit, main circuit main
module main (
  input  CLR,
  input  in_2,
  input  [11:0] in_3,
  input  en,
  input  CLK_FOR_E,
  input  [7:0] in_6,
  input  FGO,
  input  FGI,
  input  CLR_2,
  output [11:0] out_10,
  output E_CARRY,
  output R,
  output IEN,
  output [7:0] out_14
);

  wire and_1_out, and_2_out, and_3_out, and_4_out, clock_1_out, clock_2_out, d_ff_1_q, d_ff_2_q, d_ff_3_q,
       d_ff_4_q, main_1_d7, main_1_i, main_5_p2, main_6_read, main_6_write, main_7_clr, main_7_inr,
       main_7_ld, main_8_clr, main_8_inr, main_8_ld, main_9_add, main_9_and, main_9_clr, main_9_com,
       main_9_dr, main_9_inpr, main_9_inr, main_9_ld, main_9_shl, main_9_shr, main_11_inr, main_11_ld,
       multiplexer_1_out, multiplexer_2_out, not_1_out, not_2_out, not_3_out, not_4_out, not_5_out,
       not_6_out, p_out, r_out;
  wire [2:0] main_10_s0;
  wire [6:0] main_1_d0, main_5_p10;
  wire [7:0] main_13_o0;
  wire [11:0] AR_o0, bit_extender_1_out, main_1_ar;
  wire [15:0] AC_o0, DR_o0, main_3_o0, main_12_ac_out, main_16_o0, main_17_output, ram_1_data;

  and u_r (r_out, main_1_d7, not_1_out, main_5_p10[3]);
  Clock clock_1 (.out(clock_1_out));
  not not_1 (not_1_out, d_ff_3_q);
  and p (p_out, main_1_d7, d_ff_3_q, main_5_p10[3]);
  D_Flip_Flop d_ff_1 (.clk(clock_2_out), .D(FGO), .Q(d_ff_1_q), .reset(CLR_2));  // open: Qn, preset, en
  D_Flip_Flop d_ff_2 (.clk(clock_2_out), .D(FGI), .Q(d_ff_2_q), .reset(CLR_2));  // open: Qn, preset, en
  D_Flip_Flop d_ff_3 (.clk(clock_1_out), .D(main_1_i), .Q(d_ff_3_q));  // open: Qn, preset, en, reset
  not not_2 (not_2_out, d_ff_3_q);
  Clock clock_2 (.out(clock_2_out));
  IR_with_decoder_main main_1 (
    .IR(main_3_o0), .D0(main_1_d0[0]), .D1(main_1_d0[1]), .D2(main_1_d0[2]), .D3(main_1_d0[3]),
    .D4(main_1_d0[4]), .D5(main_1_d0[5]), .D6(main_1_d0[6]), .D7(main_1_d7), .AR(main_1_ar), .I(main_1_i));
  IEN_control_main main_2 (
    .Clock(clock_2_out), .p(p_out), .B7(main_1_ar[7]), .B6(main_1_ar[6]), .R(R), .T2(main_5_p10[2]), .IEN(IEN));
  r16_LD__IR__main main_3 (
    .I0(main_17_output[0]), .I1(main_17_output[1]), .I2(main_17_output[2]), .I3(main_17_output[3]),
    .I4(main_17_output[4]), .I5(main_17_output[5]), .I6(main_17_output[6]), .I7(main_17_output[7]),
    .I8(main_17_output[8]), .I9(main_17_output[9]), .I10(main_17_output[10]), .I11(main_17_output[11]),
    .I12(main_17_output[12]), .I13(main_17_output[13]), .I14(main_17_output[14]), .I15(main_17_output[15]),
    .Load(and_2_out), .CLOCK(main_5_p2), .O0(main_3_o0[0]), .O1(main_3_o0[1]), .O2(main_3_o0[2]),
    .O3(main_3_o0[3]), .O4(main_3_o0[4]), .O5(main_3_o0[5]), .O6(main_3_o0[6]), .O7(main_3_o0[7]),
    .O8(main_3_o0[8]), .O9(main_3_o0[9]), .O10(main_3_o0[10]), .O11(main_3_o0[11]), .O12(main_3_o0[12]),
    .O13(main_3_o0[13]), .O14(main_3_o0[14]), .O15(main_3_o0[15]));
  r_control_main main_4 (
    .T0(main_5_p10[0]), .T1(main_5_p10[1]), .T2(main_5_p10[2]), .IEN(IEN), .FGI(d_ff_2_q), .FGO(d_ff_1_q),
    .R(R), .Clock(clock_2_out), .R_2(R));
  and and_1 (and_1_out, main_1_ar[0], r_out);
  not not_3 (not_3_out, and_1_out);
  D_Flip_Flop d_ff_4 (.clk(main_5_p2), .D(not_3_out), .Q(d_ff_4_q));  // open: Qn, preset, en, reset
  not not_4 (not_4_out, R);
  // SEQ_COUNTER_main main_5: pin names not known; wires that end beside it: d_ff_4_q, main_5_p2, CLR, main_5_p10[6], main_5_p10[5], main_5_p10[4], main_5_p10[3], main_5_p10[2], main_5_p10[1], main_5_p10[0]
  not not_5 (not_5_out, main_1_d7);
  memory_control_main main_6 (
    .D0(main_1_d0[0]), .D1(main_1_d0[1]), .D2(main_1_d0[2]), .D3(main_1_d0[3]), .D4(main_1_d0[4]),
    .D5(main_1_d0[5]), .D6(main_1_d0[6]), .D7(main_1_d7), .I(d_ff_3_q), .R(R), .T1(main_5_p10[1]),
    .T4(main_5_p10[4]), .T3(main_5_p10[3]), .T6(main_5_p10[6]), .Write(main_6_write), .Read(main_6_read));
  and and_2 (and_2_out, not_4_out, main_5_p10[1]);
  and and_3 (and_3_out, R, main_5_p10[0]);
  and and_4 (and_4_out, main_1_ar[10], p_out);
  not not_6 (not_6_out, R);
  AR_control_main main_7 (
    .D_prime_7(not_5_out), .I(d_ff_3_q), .T3(main_5_p10[3]), .T2(main_5_p10[2]), .R(R), .T0(main_5_p10[0]),
    .D5(main_1_d0[5]), .T4(main_5_p10[4]), .LD(main_7_ld), .INR(main_7_inr), .CLR(main_7_clr));
  PC_control_main main_8 (
    .D4(main_1_d0[4]), .T4(main_5_p10[4]), .D5(main_1_d0[5]), .T5(main_5_p10[5]), .R_prime(not_4_out),
    .T1(main_5_p10[1]), .R(R), .T2(main_5_p10[2]), .D6(main_1_d0[6]), .T6(main_5_p10[6]), .r_2(r_out),
    .B4(main_1_ar[4]), .B3(main_1_ar[3]), .B2(main_1_ar[2]), .B1(main_1_ar[1]), .P(p_out), .B9(main_1_ar[9]),
    .B8(main_1_ar[8]), .R_3(R), .T1_2(main_5_p10[1]), .LD(main_8_ld), .INR(main_8_inr), .CLR(main_8_clr));
  AC_control_main main_9 (
    .D0(main_1_d0[0]), .T5(main_5_p10[5]), .D1(main_1_d0[1]), .D2(main_1_d0[2]), .T5_2(main_5_p10[5]),
    .P(p_out), .B11(main_1_ar[11]), .r(r_out), .B9(main_1_ar[9]), .B7(main_1_ar[7]), .B6(main_1_ar[6]),
    .B5(main_1_ar[5]), .B11_2(main_1_ar[11]), .AND(main_9_and), .ADD(main_9_add), .DR(main_9_dr),
    .INPR(main_9_inpr), .COM(main_9_com), .SHR(main_9_shr), .SHL(main_9_shl), .LD(main_9_ld),
    .INR(main_9_inr), .CLR(main_9_clr));
  FINAL_BUS_CONTROL_main main_10 (
    .D0_D6(main_1_d0), .D7_prime(not_5_out), .T0(main_5_p10[0]), .T1(main_5_p10[1]), .T2(main_5_p10[2]),
    .T3(main_5_p10[3]), .T4(main_5_p10[4]), .T5(main_5_p10[5]), .T6(main_5_p10[6]), .R(R),
    .R_prime(not_6_out), .I(d_ff_3_q), .p(p_out), .B10(main_1_ar[10]), .S2(main_10_s0[2]),
    .S1(main_10_s0[1]), .S0(main_10_s0[0]));
  Bit_Extender #(.in_width(16), .out_width(12)) bit_extender_1 (.in(main_17_output), .out(bit_extender_1_out));
  Multiplexer #(.enable("false")) multiplexer_1 (.in0(main_8_ld), .in1(1'b1), .out(multiplexer_1_out), .sel(en));
  DR_control_main main_11 (
    .D0(main_1_d0[0]), .T4(main_5_p10[4]), .D1(main_1_d0[1]), .D2(main_1_d0[2]), .D6(main_1_d0[6]),
    .T5(main_5_p10[5]), .LD(main_11_ld), .INR(main_11_inr));
  NEW_ALU_16_BIT_ver1_main main_12 (
    .AC_IN(AC_o0), .DR_IN(DR_o0), .AND(main_9_and), .ADD(main_9_add), .DR(main_9_dr), .IN(main_9_inpr),
    .COMP(main_9_com), .SHR(main_9_shr), .SHL(main_9_shl), .INPR(main_13_o0), .clock_for_E(CLK_FOR_E),
    .LD(1'b1), .ac_out(main_12_ac_out), .E_carry(E_CARRY));
  r8__INPR__main main_13 (
    .I0(in_6[0]), .I1(in_6[1]), .I2(in_6[2]), .I3(in_6[3]), .I4(in_6[4]), .I5(in_6[5]), .I6(in_6[6]),
    .I7(in_6[7]), .CLOCK(main_5_p2), .O0(main_13_o0[0]), .O1(main_13_o0[1]), .O2(main_13_o0[2]),
    .O3(main_13_o0[3]), .O4(main_13_o0[4]), .O5(main_13_o0[5]), .O6(main_13_o0[6]), .O7(main_13_o0[7]));
  RAM #(.addrWidth(12), .dataWidth(16), .bus("separate")) ram_1 (
    .addr(AR_o0), .din(main_17_output), .data(ram_1_data), .str(main_6_write), .clk(main_5_p2),
    .ld(main_6_read));  // open: sel, clr
  r12_LD_INR_CLR__AR_PC__main AR (
    .I0(main_17_output[0]), .I1(main_17_output[1]), .I2(main_17_output[2]), .I3(main_17_output[3]),
    .I4(main_17_output[4]), .I5(main_17_output[5]), .I6(main_17_output[6]), .I7(main_17_output[7]),
    .I8(main_17_output[8]), .I9(main_17_output[9]), .I10(main_17_output[10]), .I11(main_17_output[11]),
    .Load(main_7_ld), .INC(main_7_inr), .CLOCK(main_5_p2), .CLR(main_7_clr), .O0(AR_o0[0]), .O1(AR_o0[1]),
    .O2(AR_o0[2]), .O3(AR_o0[3]), .O4(AR_o0[4]), .O5(AR_o0[5]), .O6(AR_o0[6]), .O7(AR_o0[7]), .O8(AR_o0[8]),
    .O9(AR_o0[9]), .O10(AR_o0[10]), .O11(AR_o0[11]));
  r8_LD___OUTR__main main_14 (
    .I0(main_17_output[1]), .I1(main_17_output[2]), .I2(main_17_output[3]), .I3(main_17_output[4]),
    .I4(main_17_output[5]), .I5(main_17_output[6]), .I6(main_17_output[7]), .I7(main_17_output[8]),
    .Load(and_4_out), .CLOCK(main_5_p2), .O0(out_14[0]), .O1(out_14[1]), .O2(out_14[2]), .O3(out_14[3]),
    .O4(out_14[4]), .O5(out_14[5]), .O6(out_14[6]), .O7(out_14[7]));
  pc_main main_15 (
    .\input (bit_extender_1_out), .in_5(in_3), .En(en), .Load(multiplexer_1_out), .INC(main_8_inr),
    .CLOCK(multiplexer_2_out), .CLR(main_8_clr), .O0(out_10[0]), .O1(out_10[1]), .O2(out_10[2]),
    .O3(out_10[3]), .O4(out_10[4]), .O5(out_10[5]), .O6(out_10[6]), .O7(out_10[7]), .O8(out_10[8]),
    .O9(out_10[9]), .O10(out_10[10]), .O11(out_10[11]));
  r16_LD_INR_CLR_DR_AC_TR__main DR (
    .I0(main_17_output[0]), .I1(main_17_output[1]), .I2(main_17_output[2]), .I3(main_17_output[3]),
    .I4(main_17_output[4]), .I5(main_17_output[5]), .I6(main_17_output[6]), .I7(main_17_output[7]),
    .I8(main_17_output[8]), .I9(main_17_output[9]), .I10(main_17_output[10]), .I11(main_17_output[11]),
    .I12(main_17_output[12]), .I13(main_17_output[13]), .I14(main_17_output[14]), .I15(main_17_output[15]),
    .Load(main_11_ld), .INC(main_11_inr), .CLOCK(main_5_p2), .O0(DR_o0[0]), .O1(DR_o0[1]), .O2(DR_o0[2]),
    .O3(DR_o0[3]), .O4(DR_o0[4]), .O5(DR_o0[5]), .O6(DR_o0[6]), .O7(DR_o0[7]), .O8(DR_o0[8]), .O9(DR_o0[9]),
    .O10(DR_o0[10]), .O11(DR_o0[11]), .O12(DR_o0[12]), .O13(DR_o0[13]), .O14(DR_o0[14]), .O15(DR_o0[15]));  // open: CLR
  r16_LD_INR_CLR_DR_AC_TR__main AC (
    .I0(main_12_ac_out[0]), .I1(main_12_ac_out[1]), .I2(main_12_ac_out[2]), .I3(main_12_ac_out[3]),
    .I4(main_12_ac_out[4]), .I5(main_12_ac_out[5]), .I6(main_12_ac_out[6]), .I7(main_12_ac_out[7]),
    .I8(main_12_ac_out[8]), .I9(main_12_ac_out[9]), .I10(main_12_ac_out[10]), .I11(main_12_ac_out[11]),
    .I12(main_12_ac_out[12]), .I13(main_12_ac_out[13]), .I14(main_12_ac_out[14]), .I15(main_12_ac_out[15]),
    .Load(main_9_ld), .INC(main_9_inr), .CLOCK(main_5_p2), .CLR(main_9_clr), .O0(AC_o0[0]), .O1(AC_o0[1]),
    .O2(AC_o0[2]), .O3(AC_o0[3]), .O4(AC_o0[4]), .O5(AC_o0[5]), .O6(AC_o0[6]), .O7(AC_o0[7]), .O8(AC_o0[8]),
    .O9(AC_o0[9]), .O10(AC_o0[10]), .O11(AC_o0[11]), .O12(AC_o0[12]), .O13(AC_o0[13]), .O14(AC_o0[14]),
    .O15(AC_o0[15]));
  r16_LD_INR_CLR_DR_AC_TR__main main_16 (
    .I0(main_17_output[0]), .I1(main_17_output[1]), .I2(main_17_output[2]), .I3(main_17_output[3]),
    .I4(main_17_output[4]), .I5(main_17_output[5]), .I6(main_17_output[6]), .I7(main_17_output[7]),
    .I8(main_17_output[8]), .I9(main_17_output[9]), .I10(main_17_output[10]), .I11(main_17_output[11]),
    .I12(main_17_output[12]), .I13(main_17_output[13]), .I14(main_17_output[14]), .I15(main_17_output[15]),
    .Load(and_3_out), .CLOCK(main_5_p2), .O0(main_16_o0[0]), .O1(main_16_o0[1]), .O2(main_16_o0[2]),
    .O3(main_16_o0[3]), .O4(main_16_o0[4]), .O5(main_16_o0[5]), .O6(main_16_o0[6]), .O7(main_16_o0[7]),
    .O8(main_16_o0[8]), .O9(main_16_o0[9]), .O10(main_16_o0[10]), .O11(main_16_o0[11]), .O12(main_16_o0[12]),
    .O13(main_16_o0[13]), .O14(main_16_o0[14]), .O15(main_16_o0[15]));  // open: INC, CLR
  Clock clock_3 (.out(main_5_p2));
  bus_line_new_main main_17 (
    .selection(main_10_s0), ._001(AR_o0), ._010(out_10), ._011(DR_o0), ._100(AC_o0), ._101(main_3_o0),
    ._110(main_16_o0), ._111(ram_1_data), .\output (main_17_output));
  Multiplexer #(.enable("false")) multiplexer_2 (.in0(main_5_p2), .in1(in_2), .out(multiplexer_2_out), .sel(en));

  // Notes on the sheet:
  //   CONTROL OF SHARED BUS
  //   OUTR
  //   TR
endmodule
