// Logisim project pc.circ as structural Verilog: 1 circuit, main circuit main
module main (
  input  Load,
  input  INC,
  input  [11:0] \input ,
  input  En,
  input  [11:0] in_5,
  input  CLOCK,
  input  CLR,
  output O0,
  output O1,
  output O2,
  output O3,
  output O4,
  output O5,
  output O6,
  output O7,
  output O8,
  output O9,
  output O10,
  output O11
);

  wire and_1_out, and_2_out, and_3_out, and_4_out, and_5_out, and_6_out, and_7_out, and_8_out, and_9_out,
       and_10_out, and_11_out, and_12_out, and_13_out, and_14_out, and_15_out, and_16_out, and_17_out,
       and_18_out, and_19_out, and_20_out, and_21_out, and_22_out, and_23_out, and_24_out, and_25_out,
       and_26_out, and_27_out, and_28_out, and_29_out, and_30_out, and_31_out, and_32_out, and_33_out,
       and_34_out, and_35_out, and_36_out, not_1_out, not_2_out, not_3_out, not_4_out, not_5_out, not_6_out,
       not_7_out, not_8_out, not_9_out, not_10_out, not_11_out, not_12_out, not_13_out, or_1_out, or_2_out,
       or_3_out, or_4_out, or_5_out, or_6_out, or_7_out, or_8_out, or_9_out, or_10_out, or_11_out, or_12_out,
       or_13_out, or_14_out, or_15_out, or_16_out, or_17_out, or_18_out, or_19_out, or_20_out, or_21_out,
       or_22_out, or_23_out, or_24_out;
  wire [11:0] multiplexer_1_out;

  Multiplexer #(.width(12), .enable("false")) multiplexer_1 (
    .in0(\input ), .in1(in_5), .out(multiplexer_1_out), .sel(En));
  not not_1 (not_1_out, Load);
  not not_2 (not_2_out, multiplexer_1_out[0]);
  not not_3 (not_3_out, multiplexer_1_out[1]);
  not not_4 (not_4_out, multiplexer_1_out[2]);
  not not_5 (not_5_out, multiplexer_1_out[3]);
  not not_6 (not_6_out, multiplexer_1_out[4]);
  not not_7 (not_7_out, multiplexer_1_out[5]);
  not not_8 (not_8_out, multiplexer_1_out[6]);
  not not_9 (not_9_out, multiplexer_1_out[7]);
  not not_10 (not_10_out, multiplexer_1_out[8]);
  not not_11 (not_11_out, multiplexer_1_out[9]);
  not not_12 (not_12_out, multiplexer_1_out[10]);
  not not_13 (not_13_out, multiplexer_1_out[11]);
  and and_1 (and_1_out, not_1_out, INC);
  and and_2 (and_2_out, Load, multiplexer_1_out[0]);
  and and_3 (and_3_out, Load, not_2_out);
  and and_4 (and_4_out, Load, multiplexer_1_out[1]);
  and and_5 (and_5_out, and_1_out, O0);
  and and_6 (and_6_out, Load, not_3_out);
  and and_7 (and_7_out, Load, multiplexer_1_out[2]);
  and and_8 (and_8_out, and_5_out, O1);
  and and_9 (and_9_out, Load, not_4_out);
  and and_10 (and_10_out, Load, multiplexer_1_out[3]);
  and and_11 (and_11_out, and_8_out, O2);
  and and_12 (and_12_out, Load, not_5_out);
  and and_13 (and_13_out, Load, multiplexer_1_out[4]);
  and and_14 (and_14_out, and_11_out, O3);
  and and_15 (and_15_out, Load, not_6_out);
  and and_16 (and_16_out, Load, multiplexer_1_out[5]);
  and and_17 (and_17_out, Load, not_7_out);
  and and_18 (and_18_out, Load, multiplexer_1_out[6]);
  and and_19 (and_19_out, Load, not_8_out);
  and and_20 (and_20_out, Load, multiplexer_1_out[7]);
  and and_21 (and_21_out, Load, not_9_out);
  and and_22 (and_22_out, Load, multiplexer_1_out[8]);
  and and_23 (and_23_out, Load, not_10_out);
  and and_24 (and_24_out, Load, multiplexer_1_out[9]);
  and and_25 (and_25_out, Load, not_11_out);
  and and_26 (and_26_out, Load, multiplexer_1_out[10]);
  and and_27 (and_27_out, and_36_out, O9);
  and and_28 (and_28_out, Load, not_12_out);
  and and_29 (and_29_out, Load, multiplexer_1_out[11]);
  and and_30 (and_30_out, and_27_out, O10);
  and and_31 (and_31_out, Load, not_13_out);
  and and_32 (and_32_out, and_14_out, O4);
  and and_33 (and_33_out, and_32_out, O5);
  and and_34 (and_34_out, and_33_out, O6);
  and and_35 (and_35_out, and_34_out, O7);
  and and_36 (and_36_out, and_35_out, O8);
  or or_1 (or_1_out, and_1_out, and_2_out);
  or or_2 (or_2_out, and_1_out, and_3_out);
  or or_3 (or_3_out, and_5_out, and_4_out);
  or or_4 (or_4_out, and_5_out, and_6_out);
  or or_5 (or_5_out, and_8_out, and_7_out);
  or or_6 (or_6_out, and_8_out, and_9_out);
  or or_7 (or_7_out, and_11_out, and_10_out);
  or or_8 (or_8_out, and_11_out, and_12_out);
  or or_9 (or_9_out, and_14_out, and_13_out);
  or or_10 (or_10_out, and_14_out, and_15_out);
  or or_11 (or_11_out, and_32_out, and_16_out);
  or or_12 (or_12_out, and_32_out, and_17_out);
  or or_13 (or_13_out, and_33_out, and_18_out);
  or or_14 (or_14_out, and_33_out, and_19_out);
  or or_15 (or_15_out, and_34_out, and_20_out);
  or or_16 (or_16_out, and_34_out, and_21_out);
  or or_17 (or_17_out, and_35_out, and_22_out);
  or or_18 (or_18_out, and_35_out, and_23_out);
  or or_19 (or_19_out, and_36_out, and_24_out);
  or or_20 (or_20_out, and_36_out, and_25_out);
  or or_21 (or_21_out, and_27_out, and_26_out);
  or or_22 (or_22_out, and_27_out, and_28_out);
  or or_23 (or_23_out, and_30_out, and_29_out);
  or or_24 (or_24_out, and_30_out, and_31_out);
  J_K_Flip_Flop j_k_ff_1 (.J(or_1_out), .clk(CLOCK), .K(or_2_out), .Q(O0), .reset(CLR));  // open: Qn, preset, en
  J_K_Flip_Flop j_k_ff_2 (.J(or_3_out), .clk(CLOCK), .K(or_4_out), .Q(O1), .reset(CLR));  // open: Qn, preset, en
  J_K_Flip_Flop j_k_ff_3 (.J(or_5_out), .clk(CLOCK), .K(or_6_out), .Q(O2), .reset(CLR));  // open: Qn, preset, en
  J_K_Flip_Flop j_k_ff_4 (.J(or_7_out), .clk(CLOCK), .K(or_8_out), .Q(O3), .reset(CLR));  // open: Qn, preset, en
  J_K_Flip_Flop j_k_ff_5 (.J(or_9_out), .clk(CLOCK), .K(or_10_out), .Q(O4), .reset(CLR));  // open: Qn, preset, en
  J_K_Flip_Flop j_k_ff_6 (.J(or_11_out), .clk(CLOCK), .K(or_12_out), .Q(O5), .reset(CLR));  // open: Qn, preset, en
  J_K_Flip_Flop j_k_ff_7 (.J(or_13_out), .clk(CLOCK), .K(or_14_out), .Q(O6), .reset(CLR));  // open: Qn, preset, en
  J_K_Flip_Flop j_k_ff_8 (.J(or_15_out), .clk(CLOCK), .K(or_16_out), .Q(O7), .reset(CLR));  // open: Qn, preset, en
  J_K_Flip_Flop j_k_ff_9 (.J(or_17_out), .clk(CLOCK), .K(or_18_out), .Q(O8), .reset(CLR));  // open: Qn, preset, en
  J_K_Flip_Flop j_k_ff_10 (.J(or_19_out), .clk(CLOCK), .K(or_20_out), .Q(O9), .reset(CLR));  // open: Qn, preset, en
  J_K_Flip_Flop j_k_ff_11 (.J(or_21_out), .clk(CLOCK), .K(or_22_out), .Q(O10), .reset(CLR));  // open: Qn, preset, en
  J_K_Flip_Flop j_k_ff_12 (.J(or_23_out), .clk(CLOCK), .K(or_24_out), .Q(O11), .reset(CLR));  // open: Qn, preset, en
endmodule
