// Logisim project r16 LD (IR).circ as structural Verilog: 1 circuit, main circuit main
module main (
  input  Load,
  input  I0,
  input  I1,
  input  I2,
  input  I3,
  input  I4,
  input  I5,
  input  I6,
  input  I7,
  input  I8,
  input  I9,
  input  I10,
  input  I11,
  input  I12,
  input  I13,
  input  I14,
  input  I15,
  input  CLOCK,
  output O0,
  output O1,
  output O2,
  output O3,
  output O4,
  output O5,
  output O6,
  output O7,
  output O8,
  output O9,
  output O10,
  output O11,
  output O12,
  output O13,
  output O14,
  output O15
);

  wire and_1_out, and_2_out, and_3_out, and_4_out, and_5_out, and_6_out, and_7_out, and_8_out, and_9_out,
       and_10_out, and_11_out, and_12_out, and_13_out, and_14_out, and_15_out, and_16_out, and_17_out,
       and_18_out, and_19_out, and_20_out, and_21_out, and_22_out, and_23_out, and_24_out, and_25_out,
       and_26_out, and_27_out, and_28_out, and_29_out, and_30_out, and_31_out, and_32_out, not_1_out,
       not_2_out, not_3_out, not_4_out, not_5_out, not_6_out, not_7_out, not_8_out, not_9_out, not_10_out,
       not_11_out, not_12_out, not_13_out, not_14_out, not_15_out, not_16_out, undriven, undriven_2,
       undriven_3, undriven_4, undriven_5, undriven_6, undriven_7, undriven_8, undriven_9, undriven_10,
       undriven_11, undriven_12, undriven_13, undriven_14, undriven_15, undriven_16;

  not not_1 (not_1_out, I0);
  not not_2 (not_2_out, I1);
  not not_3 (not_3_out, I2);
  not not_4 (not_4_out, I3);
  not not_5 (not_5_out, I4);
  not not_6 (not_6_out, I5);
  not not_7 (not_7_out, I6);
  not not_8 (not_8_out, I7);
  not not_9 (not_9_out, I8);
  not not_10 (not_10_out, I9);
  not not_11 (not_11_out, I10);
  not not_12 (not_12_out, I11);
  not not_13 (not_13_out, I12);
  not not_14 (not_14_out, I13);
  not not_15 (not_15_out, I14);
  not not_16 (not_16_out, I15);
  and and_1 (and_1_out, Load, I0);
  and and_2 (and_2_out, Load, not_1_out);
  and and_3 (and_3_out, Load, I1);
  and and_4 (and_4_out, Load, not_2_out);
  and and_5 (and_5_out, Load, I2);
  and and_6 (and_6_out, Load, not_3_out);
  and and_7 (and_7_out, Load, I3);
  and and_8 (and_8_out, Load, not_4_out);
  and and_9 (and_9_out, Load, I4);
  and and_10 (and_10_out, Load, not_5_out);
  and and_11 (and_11_out, Load, I5);
  and and_12 (and_12_out, Load, not_6_out);
  and and_13 (and_13_out, Load, I6);
  and and_14 (and_14_out, Load, not_7_out);
  and and_15 (and_15_out, Load, I7);
  and and_16 (and_16_out, Load, not_8_out);
  and and_17 (and_17_out, Load, I8);
  and and_18 (and_18_out, Load, not_9_out);
  and and_19 (and_19_out, Load, I9);
  and and_20 (and_20_out, Load, not_10_out);
  and and_21 (and_21_out, Load, I10);
  and and_22 (and_22_out, Load, not_11_out);
  and and_23 (and_23_out, Load, I11);
  and and_24 (and_24_out, Load, not_12_out);
  and and_25 (and_25_out, Load, I12);
  and and_26 (and_26_out, Load, not_13_out);
  and and_27 (and_27_out, Load, I13);
  and and_28 (and_28_out, Load, not_14_out);
  and and_29 (and_29_out, Load, I14);
  and and_30 (and_30_out, Load, not_15_out);
  and and_31 (and_31_out, Load, I15);
  and and_32 (and_32_out, Load, not_16_out);
  J_K_Flip_Flop j_k_ff_1 (.J(and_1_out), .clk(CLOCK), .K(and_2_out), .Q(O0), .reset(undriven));  // open: Qn, preset, en
  J_K_Flip_Flop j_k_ff_2 (
    .J(and_3_out), .clk(CLOCK), .K(and_4_out), .Q(O1), .reset(undriven_2));  // open: Qn, preset, en
  J_K_Flip_Flop j_k_ff_3 (
    .J(and_5_out), .clk(CLOCK), .K(and_6_out), .Q(O2), .reset(undriven_3));  // open: Qn, preset, en
  J_K_Flip_Flop j_k_ff_4 (
    .J(and_7_out), .clk(CLOCK), .K(and_8_out), .Q(O3), .reset(undriven_4));  // open: Qn, preset, en
  J_K_Flip_Flop j_k_ff_5 (
    .J(and_9_out), .clk(CLOCK), .K(and_10_out), .Q(O4), .reset(undriven_5));  // open: Qn, preset, en
  J_K_Flip_Flop j_k_ff_6 (
    .J(and_11_out), .clk(CLOCK), .K(and_12_out), .Q(O5), .reset(undriven_6));  // open: Qn, preset, en
  J_K_Flip_Flop j_k_ff_7 (
    .J(and_13_out), .clk(CLOCK), .K(and_14_out), .Q(O6), .reset(undriven_7));  // open: Qn, preset, en
  J_K_Flip_Flop j_k_ff_8 (
    .J(and_15_out), .clk(CLOCK), .K(and_16_out), .Q(O7), .reset(undriven_8));  // open: Qn, preset, en
  J_K_Flip_Flop j_k_ff_9 (
    .J(and_17_out), .clk(CLOCK), .K(and_18_out), .Q(O8), .reset(undriven_9));  // open: Qn, preset, en
  J_K_Flip_Flop j_k_ff_10 (
    .J(and_19_out), .clk(CLOCK), .K(and_20_out), .Q(O9), .reset(undriven_10));  // open: Qn, preset, en
  J_K_Flip_Flop j_k_ff_11 (
    .J(and_21_out), .clk(CLOCK), .K(and_22_out), .Q(O10), .reset(undriven_11));  // open: Qn, preset, en
  J_K_Flip_Flop j_k_ff_12 (
    .J(and_23_out), .clk(CLOCK), .K(and_24_out), .Q(O11), .reset(undriven_12));  // open: Qn, preset, en
  J_K_Flip_Flop j_k_ff_13 (
    .J(and_25_out), .clk(CLOCK), .K(and_26_out), .Q(O12), .reset(undriven_13));  // open: Qn, preset, en
  J_K_Flip_Flop j_k_ff_14 (
    .J(and_27_out), .clk(CLOCK), .K(and_28_out), .Q(O13), .reset(undriven_14));  // open: Qn, preset, en
  J_K_Flip_Flop j_k_ff_15 (
    .J(and_29_out), .clk(CLOCK), .K(and_30_out), .Q(O14), .reset(undriven_15));  // open: Qn, preset, en
  J_K_Flip_Flop j_k_ff_16 (
    .J(and_31_out), .clk(CLOCK), .K(and_32_out), .Q(O15), .reset(undriven_16));  // open: Qn, preset, en
endmodule
