// Logisim project r16 LD,INR,CLR(DR,AC,TR).circ as structural Verilog: 1 circuit, main circuit main
module main (
  input  Load,
  input  INC,
  input  I0,
  input  I1,
  input  I2,
  input  I3,
  input  I4,
  input  I5,
  input  I6,
  input  I7,
  input  I8,
  input  I9,
  input  I10,
  input  I11,
  input  I12,
  input  I13,
  input  I14,
  input  I15,
  input  CLR,
  input  CLOCK,
  output O0,
  output O1,
  output O2,
  output O3,
  output O4,
  output O5,
  output O6,
  output O7,
  output O8,
  output O9,
  output O10,
  output O11,
  output O12,
  output O13,
  output O14,
  output O15
);

  wire and_1_out, and_2_out, and_3_out, and_4_out, and_5_out, and_6_out, and_7_out, and_8_out, and_9_out,
       and_10_out, and_11_out, and_12_out, and_13_out, and_14_out, and_15_out, and_16_out, and_17_out,
       and_18_out, and_19_out, and_20_out, and_21_out, and_22_out, and_23_out, and_24_out, and_25_out,
       and_26_out, and_27_out, and_28_out, and_29_out, and_30_out, and_31_out, and_32_out, and_33_out,
       and_34_out, and_35_out, and_36_out, and_37_out, and_38_out, and_39_out, and_40_out, and_41_out,
       and_42_out, and_43_out, and_44_out, and_45_out, and_46_out, and_47_out, and_48_out, not_1_out,
       not_2_out, not_3_out, not_4_out, not_5_out, not_6_out, not_7_out, not_8_out, not_9_out, not_10_out,
       not_11_out, not_12_out, not_13_out, not_14_out, not_15_out, not_16_out, not_17_out, or_1_out,
       or_2_out, or_3_out, or_4_out, or_5_out, or_6_out, or_7_out, or_8_out, or_9_out, or_10_out, or_11_out,
       or_12_out, or_13_out, or_14_out, or_15_out, or_16_out, or_17_out, or_18_out, or_19_out, or_20_out,
       or_21_out, or_22_out, or_23_out, or_24_out, or_25_out, or_26_out, or_27_out, or_28_out, or_29_out,
       or_30_out, or_31_out, or_32_out;

  not not_1 (not_1_out, I0);
  not not_2 (not_2_out, I1);
  not not_3 (not_3_out, I2);
  not not_4 (not_4_out, I3);
  not not_5 (not_5_out, I4);
  not not_6 (not_6_out, I5);
  not not_7 (not_7_out, I6);
  not not_8 (not_8_out, I7);
  not not_9 (not_9_out, I8);
  not not_10 (not_10_out, I9);
  not not_11 (not_11_out, I10);
  not not_12 (not_12_out, I11);
  not not_13 (not_13_out, I12);
  not not_14 (not_14_out, I13);
  not not_15 (not_15_out, I14);
  not not_16 (not_16_out, I15);
  not not_17 (not_17_out, Load);
  and and_1 (and_1_out, not_17_out, INC);
  and and_2 (and_2_out, Load, I0);
  and and_3 (and_3_out, Load, not_1_out);
  and and_4 (and_4_out, Load, I1);
  and and_5 (and_5_out, and_1_out, O0);
  and and_6 (and_6_out, Load, not_2_out);
  and and_7 (and_7_out, Load, I2);
  and and_8 (and_8_out, and_5_out, O1);
  and and_9 (and_9_out, Load, not_3_out);
  and and_10 (and_10_out, Load, I3);
  and and_11 (and_11_out, Load, not_4_out);
  and and_12 (and_12_out, Load, I4);
  and and_13 (and_13_out, Load, not_5_out);
  and and_14 (and_14_out, Load, I5);
  and and_15 (and_15_out, Load, not_6_out);
  and and_16 (and_16_out, Load, I6);
  and and_17 (and_17_out, Load, not_7_out);
  and and_18 (and_18_out, Load, I7);
  and and_19 (and_19_out, Load, not_8_out);
  and and_20 (and_20_out, Load, I8);
  and and_21 (and_21_out, Load, not_9_out);
  and and_22 (and_22_out, Load, I9);
  and and_23 (and_23_out, Load, not_10_out);
  and and_24 (and_24_out, Load, I10);
  and and_25 (and_25_out, Load, not_11_out);
  and and_26 (and_26_out, Load, I11);
  and and_27 (and_27_out, Load, not_12_out);
  and and_28 (and_28_out, Load, I12);
  and and_29 (and_29_out, Load, not_13_out);
  and and_30 (and_30_out, Load, I13);
  and and_31 (and_31_out, Load, not_14_out);
  and and_32 (and_32_out, Load, I14);
  and and_33 (and_33_out, Load, not_15_out);
  and and_34 (and_34_out, Load, I15);
  and and_35 (and_35_out, Load, not_16_out);
  and and_36 (and_36_out, and_8_out, O2);
  and and_37 (and_37_out, and_36_out, O3);
  and and_38 (and_38_out, and_37_out, O4);
  and and_39 (and_39_out, and_38_out, O5);
  and and_40 (and_40_out, and_39_out, O6);
  and and_41 (and_41_out, and_40_out, O7);
  and and_42 (and_42_out, and_41_out, O8);
  and and_43 (and_43_out, and_42_out, O9);
  and and_44 (and_44_out, and_43_out, O10);
  and and_45 (and_45_out, and_44_out, O11);
  and and_46 (and_46_out, and_45_out, O12);
  and and_47 (and_47_out, and_46_out, O13);
  and and_48 (and_48_out, and_47_out, O14);
  or or_1 (or_1_out, and_1_out, and_2_out);
  or or_2 (or_2_out, and_1_out, and_3_out);
  or or_3 (or_3_out, and_5_out, and_4_out);
  or or_4 (or_4_out, and_5_out, and_6_out);
  or or_5 (or_5_out, and_8_out, and_7_out);
  or or_6 (or_6_out, and_8_out, and_9_out);
  or or_7 (or_7_out, and_36_out, and_10_out);
  or or_8 (or_8_out, and_36_out, and_11_out);
  or or_9 (or_9_out, and_37_out, and_12_out);
  or or_10 (or_10_out, and_37_out, and_13_out);
  or or_11 (or_11_out, and_38_out, and_14_out);
  or or_12 (or_12_out, and_38_out, and_15_out);
  or or_13 (or_13_out, and_39_out, and_16_out);
  or or_14 (or_14_out, and_39_out, and_17_out);
  or or_15 (or_15_out, and_40_out, and_18_out);
  or or_16 (or_16_out, and_40_out, and_19_out);
  or or_17 (or_17_out, and_41_out, and_20_out);
  or or_18 (or_18_out, and_41_out, and_21_out);
  or or_19 (or_19_out, and_42_out, and_22_out);
  or or_20 (or_20_out, and_42_out, and_23_out);
  or or_21 (or_21_out, and_43_out, and_24_out);
  or or_22 (or_22_out, and_43_out, and_25_out);
  or or_23 (or_23_out, and_44_out, and_26_out);
  or or_24 (or_24_out, and_44_out, and_27_out);
  or or_25 (or_25_out, and_45_out, and_28_out);
  or or_26 (or_26_out, and_45_out, and_29_out);
  or or_27 (or_27_out, and_46_out, and_30_out);
  or or_28 (or_28_out, and_46_out, and_31_out);
  or or_29 (or_29_out, and_47_out, and_32_out);
  or or_30 (or_30_out, and_47_out, and_33_out);
  or or_31 (or_31_out, and_48_out, and_34_out);
  or or_32 (or_32_out, and_48_out, and_35_out);
  J_K_Flip_Flop j_k_ff_1 (.J(or_1_out), .clk(CLOCK), .K(or_2_out), .Q(O0), .reset(CLR));  // open: Qn, preset, en
  J_K_Flip_Flop j_k_ff_2 (.J(or_3_out), .clk(CLOCK), .K(or_4_out), .Q(O1), .reset(CLR));  // open: Qn, preset, en
  J_K_Flip_Flop j_k_ff_3 (.J(or_5_out), .clk(CLOCK), .K(or_6_out), .Q(O2), .reset(CLR));  // open: Qn, preset, en
  J_K_Flip_Flop j_k_ff_4 (.J(or_7_out), .clk(CLOCK), .K(or_8_out), .Q(O3), .reset(CLR));  // open: Qn, preset, en
  J_K_Flip_Flop j_k_ff_5 (.J(or_9_out), .clk(CLOCK), .K(or_10_out), .Q(O4), .reset(CLR));  // open: Qn, preset, en
  J_K_Flip_Flop j_k_ff_6 (.J(or_11_out), .clk(CLOCK), .K(or_12_out), .Q(O5), .reset(CLR));  // open: Qn, preset, en
  J_K_Flip_Flop j_k_ff_7 (.J(or_13_out), .clk(CLOCK), .K(or_14_out), .Q(O6), .reset(CLR));  // open: Qn, preset, en
  J_K_Flip_Flop j_k_ff_8 (.J(or_15_out), .clk(CLOCK), .K(or_16_out), .Q(O7), .reset(CLR));  // open: Qn, preset, en
  J_K_Flip_Flop j_k_ff_9 (.J(or_17_out), .clk(CLOCK), .K(or_18_out), .Q(O8), .reset(CLR));  // open: Qn, preset, en
  J_K_Flip_Flop j_k_ff_10 (.J(or_19_out), .clk(CLOCK), .K(or_20_out), .Q(O9), .reset(CLR));  // open: Qn, preset, en
  J_K_Flip_Flop j_k_ff_11 (.J(or_21_out), .clk(CLOCK), .K(or_22_out), .Q(O10), .reset(CLR));  // open: Qn, preset, en
  J_K_Flip_Flop j_k_ff_12 (.J(or_23_out), .clk(CLOCK), .K(or_24_out), .Q(O11), .reset(CLR));  // open: Qn, preset, en
  J_K_Flip_Flop j_k_ff_13 (.J(or_25_out), .clk(CLOCK), .K(or_26_out), .Q(O12), .reset(CLR));  // open: Qn, preset, en
  J_K_Flip_Flop j_k_ff_14 (.J(or_27_out), .clk(CLOCK), .K(or_28_out), .Q(O13), .reset(CLR));  // open: Qn, preset, en
  J_K_Flip_Flop j_k_ff_15 (.J(or_29_out), .clk(CLOCK), .K(or_30_out), .Q(O14), .reset(CLR));  // open: Qn, preset, en
  J_K_Flip_Flop j_k_ff_16 (.J(or_31_out), .clk(CLOCK), .K(or_32_out), .Q(O15), .reset(CLR));  // open: Qn, preset, en
endmodule
