// Logisim project r8 (INPR).circ as structural Verilog: 1 circuit, main circuit main
module main (
  input  I0,
  input  I1,
  input  I2,
  input  I3,
  input  I4,
  input  I5,
  input  I6,
  input  I7,
  input  CLOCK,
  output O0,
  output O1,
  output O2,
  output O3,
  output O4,
  output O5,
  output O6,
  output O7
);

  wire not_1_out, not_2_out, not_3_out, not_4_out, not_5_out, not_6_out, not_7_out, not_8_out, undriven,
       undriven_2, undriven_3, undriven_4, undriven_5, undriven_6, undriven_7, undriven_8;

  not not_1 (not_1_out, I0);
  not not_2 (not_2_out, I1);
  not not_3 (not_3_out, I2);
  not not_4 (not_4_out, I3);
  not not_5 (not_5_out, I4);
  not not_6 (not_6_out, I5);
  not not_7 (not_7_out, I6);
  not not_8 (not_8_out, I7);
  J_K_Flip_Flop j_k_ff_1 (.J(I0), .clk(CLOCK), .K(not_1_out), .Q(O0), .reset(undriven));  // open: Qn, preset, en
  J_K_Flip_Flop j_k_ff_2 (.J(I1), .clk(CLOCK), .K(not_2_out), .Q(O1), .reset(undriven_2));  // open: Qn, preset, en
  J_K_Flip_Flop j_k_ff_3 (.J(I2), .clk(CLOCK), .K(not_3_out), .Q(O2), .reset(undriven_3));  // open: Qn, preset, en
  J_K_Flip_Flop j_k_ff_4 (.J(I3), .clk(CLOCK), .K(not_4_out), .Q(O3), .reset(undriven_4));  // open: Qn, preset, en
  J_K_Flip_Flop j_k_ff_5 (.J(I4), .clk(CLOCK), .K(not_5_out), .Q(O4), .reset(undriven_5));  // open: Qn, preset, en
  J_K_Flip_Flop j_k_ff_6 (.J(I5), .clk(CLOCK), .K(not_6_out), .Q(O5), .reset(undriven_6));  // open: Qn, preset, en
  J_K_Flip_Flop j_k_ff_7 (.J(I6), .clk(CLOCK), .K(not_7_out), .Q(O6), .reset(undriven_7));  // open: Qn, preset, en
  J_K_Flip_Flop j_k_ff_8 (.J(I7), .clk(CLOCK), .K(not_8_out), .Q(O7), .reset(undriven_8));  // open: Qn, preset, en
endmodule
