// Logisim project r8 LD ( OUTR).circ as structural Verilog: 1 circuit, main circuit main
module main (
  input  Load,
  input  I0,
  input  I1,
  input  I2,
  input  I3,
  input  I4,
  input  I5,
  input  I6,
  input  I7,
  input  CLOCK,
  output O0,
  output O1,
  output O2,
  output O3,
  output O4,
  output O5,
  output O6,
  output O7
);

  wire and_1_out, and_2_out, and_3_out, and_4_out, and_5_out, and_6_out, and_7_out, and_8_out, and_9_out,
       and_10_out, and_11_out, and_12_out, and_13_out, and_14_out, and_15_out, and_16_out, not_1_out,
       not_2_out, not_3_out, not_4_out, not_5_out, not_6_out, not_7_out, not_8_out, undriven, undriven_2,
       undriven_3, undriven_4, undriven_5, undriven_6, undriven_7, undriven_8;

  not not_1 (not_1_out, I0);
  not not_2 (not_2_out, I1);
  not not_3 (not_3_out, I2);
  not not_4 (not_4_out, I3);
  not not_5 (not_5_out, I4);
  not not_6 (not_6_out, I5);
  not not_7 (not_7_out, I6);
  not not_8 (not_8_out, I7);
  and and_1 (and_1_out, Load, I0);
  and and_2 (and_2_out, Load, not_1_out);
  and and_3 (and_3_out, Load, I1);
  and and_4 (and_4_out, Load, not_2_out);
  and and_5 (and_5_out, Load, I2);
  and and_6 (and_6_out, Load, not_3_out);
  and and_7 (and_7_out, Load, I3);
  and and_8 (and_8_out, Load, not_4_out);
  and and_9 (and_9_out, Load, I4);
  and and_10 (and_10_out, Load, not_5_out);
  and and_11 (and_11_out, Load, I5);
  and and_12 (and_12_out, Load, not_6_out);
  and and_13 (and_13_out, Load, I6);
  and and_14 (and_14_out, Load, not_7_out);
  and and_15 (and_15_out, Load, I7);
  and and_16 (and_16_out, Load, not_8_out);
  J_K_Flip_Flop j_k_ff_1 (.J(and_1_out), .clk(CLOCK), .K(and_2_out), .Q(O0), .reset(undriven));  // open: Qn, preset, en
  J_K_Flip_Flop j_k_ff_2 (
    .J(and_3_out), .clk(CLOCK), .K(and_4_out), .Q(O1), .reset(undriven_2));  // open: Qn, preset, en
  J_K_Flip_Flop j_k_ff_3 (
    .J(and_5_out), .clk(CLOCK), .K(and_6_out), .Q(O2), .reset(undriven_3));  // open: Qn, preset, en
  J_K_Flip_Flop j_k_ff_4 (
    .J(and_7_out), .clk(CLOCK), .K(and_8_out), .Q(O3), .reset(undriven_4));  // open: Qn, preset, en
  J_K_Flip_Flop j_k_ff_5 (
    .J(and_9_out), .clk(CLOCK), .K(and_10_out), .Q(O4), .reset(undriven_5));  // open: Qn, preset, en
  J_K_Flip_Flop j_k_ff_6 (
    .J(and_11_out), .clk(CLOCK), .K(and_12_out), .Q(O5), .reset(undriven_6));  // open: Qn, preset, en
  J_K_Flip_Flop j_k_ff_7 (
    .J(and_13_out), .clk(CLOCK), .K(and_14_out), .Q(O6), .reset(undriven_7));  // open: Qn, preset, en
  J_K_Flip_Flop j_k_ff_8 (
    .J(and_15_out), .clk(CLOCK), .K(and_16_out), .Q(O7), .reset(undriven_8));  // open: Qn, preset, en
endmodule
