// Logisim project 15 bit counter.circ as structural Verilog: 1 circuit, main circuit main
module main (
  input  Load_ALWAYS_ZERO,
  input  INC,
  input  CLR,
  input  CLOCK,
  output T0,
  output T1,
  output T2,
  output T3,
  output T4,
  output T5,
  output T6,
  output T7,
  output T8,
  output T9,
  output T10,
  output T11,
  output T14,
  output T12,
  output T15,
  output T13
);

  wire and_1_out, and_2_out, and_3_out, and_4_out, and_5_out, and_6_out, and_7_out, and_8_out, and_9_out,
       and_10_out, and_11_out, and_12_out, j_k_ff_1_q, j_k_ff_2_q, j_k_ff_3_q, j_k_ff_4_q, not_1_out,
       not_2_out, not_3_out, not_4_out, not_5_out, or_1_out, or_2_out, or_3_out, or_4_out, or_5_out,
       or_6_out, or_7_out, or_8_out;

  not not_1 (not_1_out, Load_ALWAYS_ZERO);
  not not_2 (not_2_out, Load_ALWAYS_ZERO);
  not not_3 (not_3_out, Load_ALWAYS_ZERO);
  not not_4 (not_4_out, Load_ALWAYS_ZERO);
  not not_5 (not_5_out, Load_ALWAYS_ZERO);
  and and_1 (and_1_out, not_1_out, INC);
  and and_2 (and_2_out, Load_ALWAYS_ZERO, Load_ALWAYS_ZERO);
  and and_3 (and_3_out, Load_ALWAYS_ZERO, not_2_out);
  and and_4 (and_4_out, Load_ALWAYS_ZERO, Load_ALWAYS_ZERO);
  and and_5 (and_5_out, and_1_out, j_k_ff_1_q);
  and and_6 (and_6_out, Load_ALWAYS_ZERO, not_3_out);
  and and_7 (and_7_out, Load_ALWAYS_ZERO, Load_ALWAYS_ZERO);
  and and_8 (and_8_out, and_5_out, j_k_ff_2_q);
  and and_9 (and_9_out, Load_ALWAYS_ZERO, not_4_out);
  and and_10 (and_10_out, Load_ALWAYS_ZERO, Load_ALWAYS_ZERO);
  and and_11 (and_11_out, and_8_out, j_k_ff_3_q);
  and and_12 (and_12_out, Load_ALWAYS_ZERO, not_5_out);
  or or_1 (or_1_out, and_1_out, and_2_out);
  or or_2 (or_2_out, and_1_out, and_3_out);
  or or_3 (or_3_out, and_5_out, and_4_out);
  or or_4 (or_4_out, and_5_out, and_6_out);
  or or_5 (or_5_out, and_8_out, and_7_out);
  or or_6 (or_6_out, and_8_out, and_9_out);
  or or_7 (or_7_out, and_11_out, and_10_out);
  or or_8 (or_8_out, and_11_out, and_12_out);
  J_K_Flip_Flop j_k_ff_1 (
    .J(or_1_out), .clk(CLOCK), .K(or_2_out), .Q(j_k_ff_1_q), .reset(CLR));  // open: Qn, preset, en
  J_K_Flip_Flop j_k_ff_2 (
    .J(or_3_out), .clk(CLOCK), .K(or_4_out), .Q(j_k_ff_2_q), .reset(CLR));  // open: Qn, preset, en
  J_K_Flip_Flop j_k_ff_3 (
    .J(or_5_out), .clk(CLOCK), .K(or_6_out), .Q(j_k_ff_3_q), .reset(CLR));  // open: Qn, preset, en
  J_K_Flip_Flop j_k_ff_4 (
    .J(or_7_out), .clk(CLOCK), .K(or_8_out), .Q(j_k_ff_4_q), .reset(CLR));  // open: Qn, preset, en
  // decoder_main main_1: pin names not known; wires that end beside it: j_k_ff_1_q, j_k_ff_2_q, j_k_ff_3_q, j_k_ff_4_q, T0, T1, T2, T3, T4, T5, T6, T7, T8, T9, T10
endmodule
