// Logisim project 4 Bit seq count.circ as structural Verilog: 1 circuit, main circuit main
module main (
  input  Load_ALWAYS_ZERO,
  input  INC,
  input  CLR,
  output O0,
  output O1,
  output O2,
  output O3
);

  wire and_1_out, and_2_out, and_3_out, and_4_out, and_5_out, and_6_out, and_7_out, and_8_out, and_9_out,
       and_10_out, and_11_out, and_12_out, CLOCK_out, not_1_out, not_2_out, not_3_out, not_4_out, not_5_out,
       or_1_out, or_2_out, or_3_out, or_4_out, or_5_out, or_6_out, or_7_out, or_8_out;

  not not_1 (not_1_out, Load_ALWAYS_ZERO);
  not not_2 (not_2_out, Load_ALWAYS_ZERO);
  not not_3 (not_3_out, Load_ALWAYS_ZERO);
  not not_4 (not_4_out, Load_ALWAYS_ZERO);
  not not_5 (not_5_out, Load_ALWAYS_ZERO);
  and and_1 (and_1_out, not_1_out, INC);
  and and_2 (and_2_out, Load_ALWAYS_ZERO, Load_ALWAYS_ZERO);
  and and_3 (and_3_out, Load_ALWAYS_ZERO, not_2_out);
  and and_4 (and_4_out, Load_ALWAYS_ZERO, Load_ALWAYS_ZERO);
  and and_5 (and_5_out, and_1_out, O0);
  and and_6 (and_6_out, Load_ALWAYS_ZERO, not_3_out);
  and and_7 (and_7_out, Load_ALWAYS_ZERO, Load_ALWAYS_ZERO);
  and and_8 (and_8_out, and_5_out, O1);
  and and_9 (and_9_out, Load_ALWAYS_ZERO, not_4_out);
  and and_10 (and_10_out, Load_ALWAYS_ZERO, Load_ALWAYS_ZERO);
  and and_11 (and_11_out, and_8_out, O2);
  and and_12 (and_12_out, Load_ALWAYS_ZERO, not_5_out);
  or or_1 (or_1_out, and_1_out, and_2_out);
  or or_2 (or_2_out, and_1_out, and_3_out);
  or or_3 (or_3_out, and_5_out, and_4_out);
  or or_4 (or_4_out, and_5_out, and_6_out);
  or or_5 (or_5_out, and_8_out, and_7_out);
  or or_6 (or_6_out, and_8_out, and_9_out);
  or or_7 (or_7_out, and_11_out, and_10_out);
  or or_8 (or_8_out, and_11_out, and_12_out);
  Clock CLOCK (.out(CLOCK_out));
  J_K_Flip_Flop j_k_ff_1 (.J(or_1_out), .clk(CLOCK_out), .K(or_2_out), .Q(O0), .reset(CLR));  // open: Qn, preset, en
  J_K_Flip_Flop j_k_ff_2 (.J(or_3_out), .clk(CLOCK_out), .K(or_4_out), .Q(O1), .reset(CLR));  // open: Qn, preset, en
  J_K_Flip_Flop j_k_ff_3 (.J(or_5_out), .clk(CLOCK_out), .K(or_6_out), .Q(O2), .reset(CLR));  // open: Qn, preset, en
  J_K_Flip_Flop j_k_ff_4 (.J(or_7_out), .clk(CLOCK_out), .K(or_8_out), .Q(O3), .reset(CLR));  // open: Qn, preset, en
endmodule
