// Logisim project final 15 bit counter.circ as structural Verilog: 1 circuit, main circuit main
module main (
  input  incr,
  input  CLOCK,
  input  CLEAR,
  output T0,
  output T1,
  output T2,
  output T3,
  output T4,
  output T5,
  output T6,
  output T7
);

  wire and_1_out, and_2_out, and_3_out, and_4_out, and_5_out, and_6_out, and_7_out, and_8_out, and_9_out,
       j_k_ff_1_q, j_k_ff_2_q, j_k_ff_3_q, not_1_out, not_2_out, not_3_out, not_4_out, or_1_out, or_2_out,
       or_3_out, or_4_out, or_5_out, or_6_out;

  not not_1 (not_1_out, 1'b0);
  not not_2 (not_2_out, 1'b0);
  not not_3 (not_3_out, 1'b0);
  not not_4 (not_4_out, 1'b0);
  and and_1 (and_1_out, not_1_out, incr);
  and and_2 (and_2_out, 1'b0, 1'b0);
  and and_3 (and_3_out, 1'b0, not_2_out);
  and and_4 (and_4_out, 1'b0, 1'b0);
  and and_5 (and_5_out, and_1_out, j_k_ff_1_q);
  and and_6 (and_6_out, 1'b0, not_3_out);
  and and_7 (and_7_out, 1'b0, 1'b0);
  and and_8 (and_8_out, and_5_out, j_k_ff_2_q);
  and and_9 (and_9_out, 1'b0, not_4_out);
  or or_1 (or_1_out, and_1_out, and_2_out);
  or or_2 (or_2_out, and_1_out, and_3_out);
  or or_3 (or_3_out, and_5_out, and_4_out);
  or or_4 (or_4_out, and_5_out, and_6_out);
  or or_5 (or_5_out, and_8_out, and_7_out);
  or or_6 (or_6_out, and_8_out, and_9_out);
  J_K_Flip_Flop j_k_ff_1 (
    .J(or_1_out), .clk(CLOCK), .K(or_2_out), .Q(j_k_ff_1_q), .reset(CLEAR));  // open: Qn, preset, en
  J_K_Flip_Flop j_k_ff_2 (
    .J(or_3_out), .clk(CLOCK), .K(or_4_out), .Q(j_k_ff_2_q), .reset(CLEAR));  // open: Qn, preset, en
  J_K_Flip_Flop j_k_ff_3 (
    .J(or_5_out), .clk(CLOCK), .K(or_6_out), .Q(j_k_ff_3_q), .reset(CLEAR));  // open: Qn, preset, en
  decoder_main main_1 (
    ._0(j_k_ff_1_q), ._1(j_k_ff_2_q), ._2(j_k_ff_3_q), .out_4(T0), .out_5(T1), .out_6(T2), .out_7(T3),
    .out_8(T4), .out_9(T5), .out_10(T6), .out_11(T7));
endmodule
